# Fritzing sketch circuit (saved by Fritzing 1.0.2b)
perfboards: 1

parts:
  Part1 = Arduino Pro Micro (Clone)
  Part3 = Adafruit CAP1188 - 8-Key Capacitive Touch Sensor Breakout [part_number="Adafruit #1602"]
  Part4 = Adafruit CAP1188 - 8-Key Capacitive Touch Sensor Breakout [part_number="Adafruit #1602"]
  LED1 = RGB LED (com. cathode, rgb) [color="Red (633nm)" current=0.030A package="5 mm [THT]"]  # not connected

nets:
  N1: Part1.D6, Part3.RESET
  N2: Part1.D7, Part3.CS
  N3: Part1.D8, Part4.RESET
  N4: Part1.D9, Part4.CS
  N5: Part1.D16, Part3.WAKE/MOSI, Part4.WAKE/MOSI
  N6: Part1.D14, Part3.SDA/MISO, Part4.SDA/MISO
  N7: Part1.D15, Part3.SCK, Part4.SCK
  VIN: Part1.VCC, Part3.VIN, Part4.VIN
  GND: Part1.GND, Part3.ADDR, Part3.GND, Part4.ADDR, Part4.GND

custom parts:
  Adafruit CAP1188 - 8-Key Capacitive Touch Sensor Breakout: Add lots of touch sensors to your next microcontroller project with this easy-to-use 8-channel capacitive touch sensor breakout board, starring the CAP1188. This chip can handle up to 8 individual touch pads, and has a very nice feature that makes it stand out for us: it will light up the 8 onboard LEDs when the matching touch sensor fires to help you debug your sensor setup. The CAP1188 has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
